# Fritzing sketch 3StepperMotor (saved by Fritzing 0.9.7b)
breadboards: 1

parts:
  Board1 = L6470 Board [package="DIP16 [THT]"]
  Board2 = L6470 Board [package="DIP16 [THT]"]
  Board3 = L6470 Board [package="DIP16 [THT]"]
  IC1 = DIP - 8 pins [chip_label=IC package="DIP (Dual Inline) [THT]"]
  M1 = Stepper Motor - Bipolar
  M2 = Stepper Motor - Bipolar
  M3 = Stepper Motor - Bipolar
  A1 = Raspberry Pi 5

nets:
  N1: Board1.cn4_3, Board1.cn1_gnd, Board2.cn4_3, Board2.cn1_gnd, Board3.cn4_3, Board3.cn1_gnd, IC1.pin8, A1.GND, A1.Fan-PWM, A1.Fan-GND, A1.Fan-Tach
  N2: Board1.cn4_5, Board2.cn4_5, Board3.cn4_5, A1.GPIO19
  N3: Board1.cn4_6, Board2.cn4_6, Board3.cn4_6, A1.GPIO21
  N4: Board1.cn4_7, Board2.cn4_7, Board3.cn4_7, A1.GPIO20
  N5: Board1.cn4_8, A1.GPIO18
  N6: Board1.cn1_vs, Board2.cn1_vs, Board3.cn1_vs, IC1.pin5
  N7: Board1.cn2_out1a, M1.D
  N8: Board1.cn2_out2a, M1.B
  N9: Board1.cn3_out1B, M1.C
  N10: Board1.cn3_out2B, M1.A
  N11: Board2.cn4_8, A1.GPIO27
  N12: Board2.cn2_out1a, M2.D
  N13: Board2.cn2_out2a, M2.B
  N14: Board2.cn3_out1B, M2.C
  N15: Board2.cn3_out2B, M2.A
  N16: Board3.cn4_8, A1.GPIO16
  N17: Board3.cn2_out1a, M3.D
  N18: Board3.cn2_out2a, M3.B
  N19: Board3.cn3_out1B, M3.C
  N20: Board3.cn3_out2B, M3.A

notes:
  12V

custom parts:
  L6470 Board: L6470 Drive Kit
  DIP - 8 pins: A DIP stand-in part for whatever IC you want. With 8 pins on a 300mil dual inline package (DIP) footprint.
  Raspberry Pi 5: The RPi5, a faster version of the awesome Raspberry Pi4B ARM Board with 40 pin gpio.
