# Fritzing sketch A4988StepperMotor (saved by Fritzing 0.9.7b)
breadboards: 1

parts:
  M1 = Stepper Motor - Bipolar
  IC1 = DIP - 8 pins [chip_label=IC package="DIP (Dual Inline) [THT]"]
  Pololu_A1 = Pololu A4988 [package=SO16]
  A1 = Raspberry Pi 5

nets:
  N1: M1.A, Pololu_A1.1B
  N2: M1.C, Pololu_A1.1A
  N3: M1.B, Pololu_A1.2A
  N4: M1.D, Pololu_A1.2B
  N5: IC1.pin1, Pololu_A1.VMOT
  GND: IC1.pin3, Pololu_A1.GND, A1.GND
  N6: Pololu_A1.RESET, Pololu_A1.SLEEP
  N7: Pololu_A1.STEP, A1.GPIO3
  N8: Pololu_A1.DIR, A1.GPIO2
  VDD: Pololu_A1.VDD, A1.3V3

notes:
  12V

custom parts:
  DIP - 8 pins: A DIP stand-in part for whatever IC you want. With 8 pins on a 300mil dual inline package (DIP) footprint.
  Raspberry Pi 5: The RPi5, a faster version of the awesome Raspberry Pi4B ARM Board with 40 pin gpio.
