# Fritzing sketch L6470StepperMotor (saved by Fritzing 0.9.7b)

parts:
  IC3 = DIP - 8 pins [chip_label=IC package="DIP (Dual Inline) [THT]"]
  Board1 = L6470 Board [package="DIP16 [THT]"]
  M1 = Stepper Motor - Bipolar
  A1 = Raspberry Pi 5

nets:
  N1: IC3.pin6, Board1.cn1_vs
  N2: IC3.pin8, Board1.cn1_gnd
  N3: Board1.cn4_3, A1.GND
  N4: Board1.cn4_5, A1.GPIO9
  N5: Board1.cn4_6, A1.GPIO11
  N6: Board1.cn4_7, A1.GPIO10
  N7: Board1.cn4_8, A1.GPIO8
  N8: Board1.cn2_out1a, M1.A
  N9: Board1.cn2_out2a, M1.C
  N10: Board1.cn3_out1B, M1.B
  N11: Board1.cn3_out2B, M1.D

notes:
  JP1は1-2, 3-4をショート
  12V

custom parts:
  DIP - 8 pins: A DIP stand-in part for whatever IC you want. With 8 pins on a 300mil dual inline package (DIP) footprint.
  L6470 Board: L6470 Drive Kit
  Raspberry Pi 5: The RPi5, a faster version of the awesome Raspberry Pi4B ARM Board with 40 pin gpio.
