# Fritzing sketch L6470StepperMotor_0 (saved by Fritzing 0.9.7b)
breadboards: 1

parts:
  IC3 = DIP - 8 pins [chip_label=IC package="DIP (Dual Inline) [THT]"]
  Board1 = L6470 Board [package="DIP16 [THT]"]
  M1 = Stepper Motor - Bipolar
  A1 = Raspberry Pi 5

nets:
  N1: IC3.pin5, Board1.cn1_vs
  N2: IC3.pin8, Board1.cn4_3, Board1.cn1_gnd, A1.GND
  N3: Board1.cn4_5, A1.GPIO9
  N4: Board1.cn4_6, A1.GPIO11
  N5: Board1.cn4_7, A1.GPIO10
  N6: Board1.cn4_8, A1.GPIO8
  N7: Board1.cn2_out1a, M1.A
  N8: Board1.cn2_out2a, M1.C
  N9: Board1.cn3_out1B, M1.B
  N10: Board1.cn3_out2B, M1.D

notes:
  JP1は1-2, 3-4をショート
  12V

custom parts:
  DIP - 8 pins: A DIP stand-in part for whatever IC you want. With 8 pins on a 300mil dual inline package (DIP) footprint.
  L6470 Board: L6470 Drive Kit
  Raspberry Pi 5: The RPi5, a faster version of the awesome Raspberry Pi4B ARM Board with 40 pin gpio.
