# Fritzing sketch LChika (saved by Fritzing 0.9.7b)
breadboards: 1

parts:
  A1 = Raspberry Pi 5
  R1 = Resistor [tolerance=±5% power=0.25 resistance=330 package=THT]
  LED1 = LED - 5mm [color="Red (633nm)" current=0.030 package="5 mm [THT]"]

nets:
  N1: A1.GND, LED1.cathode
  N2: A1.GPIO25, R1.Pin_0
  N3: R1.Pin_1, LED1.anode

custom parts:
  Raspberry Pi 5: The RPi5, a faster version of the awesome Raspberry Pi4B ARM Board with 40 pin gpio.
