# Fritzing sketch OmniMouse_Circuit (saved by Fritzing 0.9.7b)

parts:
  A2 = XY-3606
  U1 = SPDT Slide Switch [package=ayz0202]
  U2 = SPDT Slide Switch [package=ayz0202]
  IC1 = DIP - 8 pins [chip_label=IC package="DIP (Dual Inline) [THT]"]
  A3 = Raspberry Pi 5
  U3 = Header 6 [package=1x06_smd_straight_alt]
  U4 = Header 6 [package=1x06_smd_straight_alt]
  U5 = Header 6 [package=1x06_smd_straight_alt]
  Board1 = L6470 Board [package="DIP16 [THT]"]
  Board2 = L6470 Board [package="DIP16 [THT]"]
  Board3 = L6470 Board [package="DIP16 [THT]"]
  U6 = Header 6 [package=1x06_smd_straight_alt]
  U7 = Header 6 [package=1x06_smd_straight_alt]
  U8 = Header 6 [package=1x06_smd_straight_alt]
  M1 = Stepper Motor - Bipolar
  M2 = Stepper Motor - Bipolar
  M3 = Stepper Motor - Bipolar
  BATT1 = LiPoly Battery (1300mAh)

nets:
  N1: A2.Pin_1, U1.3
  N2: A2.Pin_2, A2.Pin_3, IC1.pin4, A3.GND, U3.1, U3.2, U3.3, U3.4, U3.6, U5.1, U5.2, U5.3, U5.4, U5.6, Board1.cn4_3, Board1.cn1_gnd, Board2.cn4_3, Board2.cn1_gnd, Board3.cn4_3, Board3.cn1_gnd
  N3: A2.Pin_4, A3.5V, A3.Fan-5V
  N4: U2.3, U4.1, U4.2, U4.3, U4.4, Board1.cn1_vs, Board2.cn1_vs, Board3.cn1_vs
  N5: U2.2, IC1.pin1
  N6: IC1.pin5, BATT1.positive
  N7: IC1.pin8, BATT1.negative
  N8: A3.GPIO18, Board1.cn4_8
  N9: A3.GPIO27, Board2.cn4_8
  N10: A3.GPIO19, Board1.cn4_5, Board2.cn4_5, Board3.cn4_5, U7.2, U7.3, U7.4, U7.6
  N11: A3.GPIO16, Board3.cn4_8
  N12: A3.GPIO20, Board1.cn4_7, Board2.cn4_7, Board3.cn4_7, U8.2, U8.3, U8.4, U8.6
  N13: A3.GPIO21, Board1.cn4_6, Board2.cn4_6, Board3.cn4_6, U6.2, U6.3, U6.4, U6.6
  N14: Board1.cn2_out1a, M1.D
  N15: Board1.cn2_out2a, M1.B
  N16: Board1.cn3_out1B, M1.C
  N17: Board1.cn3_out2B, M1.A
  N18: Board2.cn2_out1a, M2.D
  N19: Board2.cn2_out2a, M2.B
  N20: Board2.cn3_out1B, M2.C
  N21: Board2.cn3_out2B, M2.A
  N22: Board3.cn2_out1a, M3.D
  N23: Board3.cn2_out2a, M3.B
  N24: Board3.cn3_out1B, M3.C
  N25: Board3.cn3_out2B, M3.A

custom parts:
  XY-3606: 24V/12V turn 5V 5A power module, DC-DC XY-3606 Power Converter Super LM2596S.
  DIP - 8 pins: A DIP stand-in part for whatever IC you want. With 8 pins on a 300mil dual inline package (DIP) footprint.
  Raspberry Pi 5: The RPi5, a faster version of the awesome Raspberry Pi4B ARM Board with 40 pin gpio.
  L6470 Board: L6470 Drive Kit
  LiPoly Battery (1300mAh): Lithium Ion Polymer Battery (1300mAh)
