# Fritzing sketch ReadAdc (saved by Fritzing 0.9.7b)
breadboards: 1

parts:
  ADC1 = MCP3008 [package=dil16]
  パーツ1 = Parallax 2-Axis Joystick
  A1 = Raspberry Pi 5

nets:
  N1: ADC1.CH0, パーツ1.U/D_Out
  N2: ADC1.DGND, ADC1.AGND, パーツ1.GND#8, A1.GND, A1.Fan-GND
  N3: ADC1.CS/SHDN, A1.GPIO8
  N4: ADC1.Din, A1.GPIO10
  N5: ADC1.Dout, A1.GPIO9
  N6: ADC1.CLK, A1.GPIO11
  VDD: ADC1.VREF, ADC1.VDD, パーツ1.U/D_Vcc, A1.3V3

custom parts:
  Parallax 2-Axis Joystick: Description: This is the Parallax 2-Axis Joystick. It contains a spring return thumb joystick mounted to a breakout board. The breakout board breaks out the joysticks connections to .1" pin headers. The joystick's connections are duplicated on both sides of the board for easy use. This part can easily be used on a breadboard due to the .1" pin headers, but can also be soldered into any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
  Raspberry Pi 5: The RPi5, a faster version of the awesome Raspberry Pi4B ARM Board with 40 pin gpio.
