# Fritzing sketch RunOnBattery (saved by Fritzing 0.9.7b)

parts:
  A1 = XY-3606
  A2 = Raspberry Pi 5
  BATT1 = LiPoly Battery (1300mAh)

nets:
  N1: A1.Pin_1, BATT1.positive
  N2: A1.Pin_2, A1.Pin_3, A2.GND, BATT1.negative
  N3: A1.Pin_4, A2.5V, A2.Fan-5V

notes:
  12V to 5V

custom parts:
  XY-3606: 24V/12V turn 5V 5A power module, DC-DC XY-3606 Power Converter Super LM2596S.
  Raspberry Pi 5: The RPi5, a faster version of the awesome Raspberry Pi4B ARM Board with 40 pin gpio.
  LiPoly Battery (1300mAh): Lithium Ion Polymer Battery (1300mAh)
