# Fritzing sketch OmniMouse_Circuit (saved by Fritzing 1.0.5)
stripboards: 1

parts:
  Power_plug1 = Power plug
  S1 = Toggle Switch [package=THT]
  S2 = Toggle Switch [package=THT]
  A6 = XY-3606
  A7 = Raspberry Pi 5
  Board1 = L6470 Board [package="DIP16 [THT]"]
  Board2 = L6470 Board [package="DIP16 [THT]"]
  Board3 = L6470 Board [package="DIP16 [THT]"]
  M3 = Stepper Motor - Bipolar
  M2 = Stepper Motor - Bipolar
  M4 = Stepper Motor - Bipolar

nets:
  GND: Power_plug1.GND, A6.Pin_2, A6.Pin_3, A7.GND, A7.Fan-GND, Board1.cn4_3, Board1.cn1_gnd, Board2.cn4_3, Board2.cn1_gnd, Board3.cn4_3, Board3.cn1_gnd
  N1: Power_plug1.VCC, S1.L2, S2.L1
  N2: S1.COM, A6.Pin_1
  N3: S2.L2, Board1.cn1_vs, Board2.cn1_vs, Board3.cn1_vs
  N4: A6.Pin_4, A7.5V
  N5: A7.GPIO10, Board3.cn4_7
  N6: A7.GPIO9, Board1.cn4_5
  N7: A7.GPIO11, Board1.cn4_6, Board2.cn4_6, Board3.cn4_6
  N8: A7.GPIO8, Board1.cn4_8, Board2.cn4_8, Board3.cn4_8
  N9: Board1.cn4_7, Board2.cn4_5
  N10: Board1.cn2_out1a, M4.C
  N11: Board1.cn2_out2a, M4.A
  N12: Board1.cn3_out1B, M4.D
  N13: Board1.cn3_out2B, M4.B
  N14: Board2.cn4_7, Board3.cn4_5
  N15: Board2.cn2_out1a, M3.C
  N16: Board2.cn2_out2a, M3.A
  N17: Board2.cn3_out1B, M3.D
  N18: Board2.cn3_out2B, M3.B
  N19: Board3.cn2_out1a, M2.C
  N20: Board3.cn2_out2a, M2.A
  N21: Board3.cn3_out1B, M2.D
  N22: Board3.cn3_out2B, M2.B

custom parts:
  XY-3606: 24V/12V turn 5V 5A power module, DC-DC XY-3606 Power Converter Super LM2596S.
  Raspberry Pi 5: The RPi5, a faster version of the awesome Raspberry Pi4B ARM Board with 40 pin gpio.
  L6470 Board: L6470 Drive Kit
